# Fritzing sketch ultrasonic_distance (saved by Fritzing 0.9.3b)
breadboards: 1

parts:
  Part1 = Arduino Uno (Rev3)
  HC-SR04_Sensor_1 = HC-SR04 Ultrasonic Distance Sensor
  LED1 = LED - 5mm [color="Red (633nm)" package="5 mm [THT]"]
  R1 = Resistor [tolerance=±5% resistance=220 package=THT]
  R2 = Resistor [tolerance=±5% resistance=220 package=THT]
  R3 = Resistor [tolerance=±5% resistance=220 package=THT]
  R4 = Resistor [tolerance=±5% resistance=220 package=THT]
  LED2 = LED - 5mm [color="Red (633nm)" package="5 mm [THT]"]
  LED3 = LED - 5mm [color="Red (633nm)" package="5 mm [THT]"]
  LED4 = LED - 5mm [color="Red (633nm)" package="5 mm [THT]"]

nets:
  N1: Part1.D8, LED1.cathode
  N2: Part1.D9_PWM, LED2.cathode
  N3: Part1.D10_PWM/SS, LED3.cathode
  N4: Part1.D11_PWM/MOSI, LED4.cathode
  N5: Part1.D12/MISO, HC-SR04_Sensor_1.ECHO
  N6: Part1.D13/SCK, HC-SR04_Sensor_1.TRIG
  GND: Part1.GND, HC-SR04_Sensor_1.GND, R1.Pin_0, R2.Pin_0, R3.Pin_0, R4.Pin_0
  5V: Part1.5V, HC-SR04_Sensor_1.VCC
  N7: LED1.anode, R1.Pin_1
  N8: R2.Pin_1, LED2.anode
  N9: R3.Pin_1, LED3.anode
  N10: R4.Pin_1, LED4.anode
